// Logisim project pipelined_datapath.circ as structural Verilog: 12 circuits, main circuit main
module main (
);

  wire alu_1_z, and_1_out, clock_1_out, clocks_1_out_1, control_unit_1_cbr, control_unit_1_linkreg,
       control_unit_1_memread, control_unit_1_memwrite, control_unit_1_pbr, control_unit_1_reg2loc,
       control_unit_1_regwrite, control_unit_1_ubr, exme_1_out_memread, exme_1_out_memwrite,
       hazard_detection_unit_1_hazardsignal, idex_1_out_alusrc, idex_1_out_cbr, idex_1_out_ubr,
       mewb_1_out_regwrite, not_1_out, or_2_out;
  wire [1:0] forwarding_unit_1_fa, forwarding_unit_1_fb, idex_1_out_me, mewb_1_out_memtoreg, or_1_out;
  wire [2:0] control_unit_1_aluop, exme_1_out_wb, idex_1_out_aluop, idex_1_out_wb;
  wire [3:0] alu_control_1_action;
  wire [4:0] exme_1_out_writereg, idex_1_out_readreg1, idex_1_out_readreg2, idex_1_out_writereg,
       ifid_1_out_rd, ifid_1_out_rm, ifid_1_out_rn, ifid_1_out_rt, mewb_1_out_writereg, multiplexer_1_out;
  wire [10:0] adder_1_out, adder_2_out, alu_1_aluout, exme_1_out_nextpc, idex_1_out_imm, idex_1_out_nextpc,
       idex_1_out_opcode, idex_1_out_pc, ifid_1_out_imm, ifid_1_out_nextpc, ifid_1_out_opcode, ifid_1_out_pc,
       mewb_1_out_nextpc, multiplexer_2_out, multiplexer_6_out, PC_q;
  wire [31:0] bit_extender_1_out, bit_extender_2_out, exme_1_out_aluout, exme_1_out_regdata2,
       idex_1_out_regdata1, idex_1_out_regdata2, Instruction_Memory_data, mewb_1_out_aluout,
       mewb_1_out_readdatam, multiplexer_3_out, multiplexer_4_out, multiplexer_5_out, multiplexer_7_out,
       ram_1_dout, register_file_1_regdata1, register_file_1_regdata2;
  wire [31:11] alu_1_aluout_2;

  Clocks clocks_1 (.out_1(clocks_1_out_1));
  Register #(.width(11)) PC (.D(multiplexer_6_out), .en(1'b1), .clk(clocks_1_out_1), .Q(PC_q));  // open: clr
  ROM #(.addrWidth(11), .dataWidth(32)) Instruction_Memory (.addr(PC_q), .data(Instruction_Memory_data));
  Adder #(.width(11)) adder_1 (.a(PC_q), .b(11'h1), .out(adder_1_out));  // open: cin, cout
  IFID ifid_1 (
    .opcode(Instruction_Memory_data[31:21]), .imm(Instruction_Memory_data[20:10]),
    .Rd(Instruction_Memory_data[4:0]), .Rt(Instruction_Memory_data[4:0]),
    .Rm(Instruction_Memory_data[20:16]), .Rn(Instruction_Memory_data[9:5]), .PC(PC_q), .nextPC(adder_1_out),
    .out_opcode(ifid_1_out_opcode), .out_imm(ifid_1_out_imm), .out_Rd(ifid_1_out_rd), .out_Rt(ifid_1_out_rt),
    .out_Rm(ifid_1_out_rm), .out_Rn(ifid_1_out_rn), .out_PC(ifid_1_out_pc), .out_nextPC(ifid_1_out_nextpc));
  Multiplexer #(.width(5)) multiplexer_1 (
    .in0(ifid_1_out_rt), .in1(ifid_1_out_rm), .out(multiplexer_1_out), .sel(control_unit_1_reg2loc));
  Hazard_Detection_Unit hazard_detection_unit_1 (
    .IFID_ReadReg1(ifid_1_out_rn), .IDEX_WriteReg(idex_1_out_writereg), .IFID_ReadReg2(multiplexer_1_out),
    .IDEX_MemRead(idex_1_out_me[1]), .IDEX_Br(or_2_out), .HazardSignal(hazard_detection_unit_1_hazardsignal));
  register_file register_file_1 (
    .ReadReg1(ifid_1_out_rn), .ReadReg2(multiplexer_1_out), .WriteReg(mewb_1_out_writereg),
    .RegWrite(mewb_1_out_regwrite), .RegDataW(multiplexer_7_out), .RegData1(register_file_1_regdata1),
    .RegData2(register_file_1_regdata2));
  Multiplexer #(.width(11)) multiplexer_2 (
    .in0(ifid_1_out_opcode), .in1({11{1'b0}}), .out(multiplexer_2_out),
    .sel(hazard_detection_unit_1_hazardsignal));
  Control_Unit control_unit_1 (
    .opcode(multiplexer_2_out), .LinkReg(control_unit_1_linkreg), .RegWrite(control_unit_1_regwrite),
    .MemWrite(control_unit_1_memwrite), .MemRead(control_unit_1_memread), .Reg2Loc(control_unit_1_reg2loc),
    .ALUop(control_unit_1_aluop), .UBr(control_unit_1_ubr), .CBr(control_unit_1_cbr), .PBr(control_unit_1_pbr));
  IDEX idex_1 (
    .opcode(ifid_1_out_opcode), .imm(ifid_1_out_imm), .WriteReg(ifid_1_out_rd),
    .RegData1(register_file_1_regdata1), .RegData2(register_file_1_regdata2), .ReadReg1(ifid_1_out_rn),
    .ReadReg2(multiplexer_1_out), .PC(ifid_1_out_pc), .nextPC(ifid_1_out_nextpc),
    .ALUsrc(control_unit_1_reg2loc), .ALUop(control_unit_1_aluop), .UBr(control_unit_1_ubr),
    .CBr(control_unit_1_cbr), .PBr(control_unit_1_pbr), .MemWrite(control_unit_1_memwrite),
    .MemRead(control_unit_1_memread), .LinkReg(control_unit_1_linkreg), .RegWrite(control_unit_1_regwrite),
    .out_opcode(idex_1_out_opcode), .out_imm(idex_1_out_imm), .out_WriteReg(idex_1_out_writereg),
    .out_RegData1(idex_1_out_regdata1), .out_RegData2(idex_1_out_regdata2),
    .out_ReadReg1(idex_1_out_readreg1), .out_ReadReg2(idex_1_out_readreg2), .out_PC(idex_1_out_pc),
    .out_nextPC(idex_1_out_nextpc), .out_ALUsrc(idex_1_out_alusrc), .out_ALUop(idex_1_out_aluop),
    .out_UBr(idex_1_out_ubr), .out_CBr(idex_1_out_cbr), .out_PBr(or_1_out[1]), .out_ME(idex_1_out_me),
    .out_WB(idex_1_out_wb));
  ALU_Control alu_control_1 (.ALUop(idex_1_out_aluop), .action(alu_control_1_action));
  assign bit_extender_1_out = {{21{idex_1_out_imm[10]}}, idex_1_out_imm};  // Bit_Extender bit_extender_1
  not not_1 (not_1_out, idex_1_out_alusrc);
  Multiplexer #(.width(32)) multiplexer_3 (
    .in0(bit_extender_1_out), .in1(idex_1_out_regdata2), .out(multiplexer_3_out), .sel(not_1_out));
  Adder #(.width(11)) adder_2 (.a(idex_1_out_pc), .b(idex_1_out_imm), .out(adder_2_out));  // open: cin, cout
  Forwarding_Unit forwarding_unit_1 (
    .EXME_RegWrite(exme_1_out_wb[2]), .EXME_WriteReg(exme_1_out_writereg),
    .IDEX_ReadReg1(idex_1_out_readreg1), .MEWB_WriteReg(mewb_1_out_writereg),
    .MEWB_RegWrite(mewb_1_out_regwrite), .IDEX_ReadReg2(idex_1_out_readreg2), .FA(forwarding_unit_1_fa),
    .FB(forwarding_unit_1_fb));
  Multiplexer #(.select(2), .width(32)) multiplexer_4 (
    .in0(multiplexer_3_out), .in1(exme_1_out_aluout), .in2(multiplexer_7_out), .out(multiplexer_4_out),
    .sel(forwarding_unit_1_fb));  // open: in3
  and and_1 (and_1_out, idex_1_out_cbr, alu_1_z);
  ALU alu_1 (
    .A(multiplexer_4_out), .B(multiplexer_5_out), .action(alu_control_1_action),
    .ALUout({alu_1_aluout_2, alu_1_aluout}), .Z(alu_1_z));
  Multiplexer #(.select(2), .width(32)) multiplexer_5 (
    .in0(idex_1_out_regdata1), .in1(exme_1_out_aluout), .in2(multiplexer_7_out), .out(multiplexer_5_out),
    .sel(forwarding_unit_1_fa));  // open: in3
  or or_1 (or_1_out[0], idex_1_out_ubr, and_1_out);
  or or_2 (or_2_out, or_1_out[0], or_1_out[1]);
  Multiplexer #(.select(2), .width(11)) multiplexer_6 (
    .in0(idex_1_out_nextpc), .in1(adder_2_out), .in2(alu_1_aluout), .out(multiplexer_6_out), .sel(or_1_out));  // open: in3
  EXME exme_1 (
    .WriteReg(idex_1_out_writereg), .ALUout({alu_1_aluout_2, alu_1_aluout}), .RegData2(idex_1_out_regdata2),
    .nextPC(idex_1_out_nextpc), .ME(idex_1_out_me), .WB(idex_1_out_wb), .out_WriteReg(exme_1_out_writereg),
    .out_ALUout(exme_1_out_aluout), .out_RegData2(exme_1_out_regdata2), .out_nextPC(exme_1_out_nextpc),
    .out_MemWrite(exme_1_out_memwrite), .out_MemRead(exme_1_out_memread), .out_WB(exme_1_out_wb));
  RAM #(.addrWidth(11), .dataWidth(32)) ram_1 (
    .addr(exme_1_out_aluout[10:0]), .we(exme_1_out_memwrite), .oe(exme_1_out_memread), .clk(clock_1_out),
    .din(exme_1_out_regdata2), .dout(ram_1_dout));
  Clock clock_1 (.out(clock_1_out));
  MEWB mewb_1 (
    .WriteReg(exme_1_out_writereg), .ALUout(exme_1_out_aluout), .ReadDataM(ram_1_dout),
    .nextPC(exme_1_out_nextpc), .WB(exme_1_out_wb), .out_WriteReg(mewb_1_out_writereg),
    .out_ALUout(mewb_1_out_aluout), .out_ReadDataM(mewb_1_out_readdatam), .out_nextPC(mewb_1_out_nextpc),
    .out_MemToReg(mewb_1_out_memtoreg[0]), .out_LinkReg(mewb_1_out_memtoreg[1]),
    .out_RegWrite(mewb_1_out_regwrite));
  assign bit_extender_2_out = {{21{mewb_1_out_nextpc[10]}}, mewb_1_out_nextpc};  // Bit_Extender bit_extender_2
  Multiplexer #(.select(2), .width(32)) multiplexer_7 (
    .in0(mewb_1_out_aluout), .in1(mewb_1_out_readdatam), .in2(bit_extender_2_out), .out(multiplexer_7_out),
    .sel(mewb_1_out_memtoreg));  // open: in3

  // Notes on the sheet:
  //   contents of Instruction_Memory (hex, n*v repeats v):
  //   0 a40e041 e40e041 300ff41e
endmodule

module register_file (
  input  [31:0] RegDataW,
  input  RegWrite,
  input  [4:0] ReadReg1,
  input  [4:0] WriteReg,
  input  [4:0] ReadReg2,
  output [31:0] RegData1,
  output [31:0] RegData2
);

  wire and_1_out, and_2_out, and_3_out, and_4_out, and_5_out, and_6_out, and_7_out, and_8_out, and_9_out,
       and_10_out, and_11_out, and_12_out, and_13_out, and_14_out, and_15_out, and_16_out, and_17_out,
       and_18_out, and_19_out, and_20_out, and_21_out, and_22_out, and_23_out, and_24_out, and_25_out,
       and_26_out, and_27_out, and_28_out, and_29_out, and_30_out, and_31_out, clocks_1_out_1,
       decoder_1_out0, decoder_1_out1, decoder_1_out2, decoder_1_out3, decoder_1_out4, decoder_1_out5,
       decoder_1_out6, decoder_1_out7, decoder_1_out8, decoder_1_out9, decoder_1_out10, decoder_1_out11,
       decoder_1_out12, decoder_1_out13, decoder_1_out14, decoder_1_out15, decoder_1_out16, decoder_1_out17,
       decoder_1_out18, decoder_1_out19, decoder_1_out20, decoder_1_out21, decoder_1_out22, decoder_1_out23,
       decoder_1_out24, decoder_1_out25, decoder_1_out26, decoder_1_out27, decoder_1_out28, decoder_1_out29,
       decoder_1_out30;
  wire [31:0] X0_q, X1_q, X2_q, X3_q, X4_q, X5_q, X6_q, X7_q, X8_q, X9_q, X10_q, X11_q, X12_q, X13_q, X14_q,
       X15_q, X16_q, X17_q, X18_q, X19_q, X20_q, X21_q, X22_q, X23_q, X24_q, X25_q, X26_q, X27_q, X28_q,
       X29_q, X30_q, X31_q;

  Decoder #(.select(5)) decoder_1 (
    .out0(decoder_1_out0), .out1(decoder_1_out1), .out2(decoder_1_out2), .out3(decoder_1_out3),
    .out4(decoder_1_out4), .out5(decoder_1_out5), .out6(decoder_1_out6), .out7(decoder_1_out7),
    .out8(decoder_1_out8), .out9(decoder_1_out9), .out10(decoder_1_out10), .out11(decoder_1_out11),
    .out12(decoder_1_out12), .out13(decoder_1_out13), .out14(decoder_1_out14), .out15(decoder_1_out15),
    .out16(decoder_1_out16), .out17(decoder_1_out17), .out18(decoder_1_out18), .out19(decoder_1_out19),
    .out20(decoder_1_out20), .out21(decoder_1_out21), .out22(decoder_1_out22), .out23(decoder_1_out23),
    .out24(decoder_1_out24), .out25(decoder_1_out25), .out26(decoder_1_out26), .out27(decoder_1_out27),
    .out28(decoder_1_out28), .out29(decoder_1_out29), .out30(decoder_1_out30), .sel(WriteReg));  // open: out31, en
  and and_1 (and_1_out, RegWrite, decoder_1_out0);
  and and_2 (and_2_out, RegWrite, decoder_1_out1);
  and and_3 (and_3_out, RegWrite, decoder_1_out2);
  and and_4 (and_4_out, RegWrite, decoder_1_out3);
  and and_5 (and_5_out, RegWrite, decoder_1_out4);
  and and_6 (and_6_out, RegWrite, decoder_1_out5);
  and and_7 (and_7_out, RegWrite, decoder_1_out6);
  and and_8 (and_8_out, RegWrite, decoder_1_out7);
  and and_9 (and_9_out, RegWrite, decoder_1_out8);
  and and_10 (and_10_out, RegWrite, decoder_1_out9);
  and and_11 (and_11_out, RegWrite, decoder_1_out10);
  and and_12 (and_12_out, RegWrite, decoder_1_out11);
  and and_13 (and_13_out, RegWrite, decoder_1_out12);
  and and_14 (and_14_out, RegWrite, decoder_1_out13);
  and and_15 (and_15_out, RegWrite, decoder_1_out14);
  and and_16 (and_16_out, RegWrite, decoder_1_out15);
  and and_17 (and_17_out, RegWrite, decoder_1_out16);
  and and_18 (and_18_out, RegWrite, decoder_1_out17);
  and and_19 (and_19_out, RegWrite, decoder_1_out18);
  and and_20 (and_20_out, RegWrite, decoder_1_out19);
  and and_21 (and_21_out, RegWrite, decoder_1_out20);
  and and_22 (and_22_out, RegWrite, decoder_1_out21);
  and and_23 (and_23_out, RegWrite, decoder_1_out22);
  and and_24 (and_24_out, RegWrite, decoder_1_out23);
  and and_25 (and_25_out, RegWrite, decoder_1_out24);
  and and_26 (and_26_out, RegWrite, decoder_1_out25);
  and and_27 (and_27_out, RegWrite, decoder_1_out26);
  and and_28 (and_28_out, RegWrite, decoder_1_out27);
  and and_29 (and_29_out, RegWrite, decoder_1_out28);
  and and_30 (and_30_out, RegWrite, decoder_1_out29);
  and and_31 (and_31_out, RegWrite, decoder_1_out30);
  Clocks clocks_1 (.out_1(clocks_1_out_1));
  Register #(.width(32)) X0 (.D(RegDataW), .en(and_1_out), .clk(clocks_1_out_1), .Q(X0_q));  // open: clr
  Register #(.width(32)) X1 (.D(RegDataW), .en(and_2_out), .clk(clocks_1_out_1), .Q(X1_q));  // open: clr
  Register #(.width(32)) X2 (.D(RegDataW), .en(and_3_out), .clk(clocks_1_out_1), .Q(X2_q));  // open: clr
  Register #(.width(32)) X3 (.D(RegDataW), .en(and_4_out), .clk(clocks_1_out_1), .Q(X3_q));  // open: clr
  Register #(.width(32)) X4 (.D(RegDataW), .en(and_5_out), .clk(clocks_1_out_1), .Q(X4_q));  // open: clr
  Register #(.width(32)) X5 (.D(RegDataW), .en(and_6_out), .clk(clocks_1_out_1), .Q(X5_q));  // open: clr
  Register #(.width(32)) X6 (.D(RegDataW), .en(and_7_out), .clk(clocks_1_out_1), .Q(X6_q));  // open: clr
  Register #(.width(32)) X7 (.D(RegDataW), .en(and_8_out), .clk(clocks_1_out_1), .Q(X7_q));  // open: clr
  Register #(.width(32)) X8 (.D(RegDataW), .en(and_9_out), .clk(clocks_1_out_1), .Q(X8_q));  // open: clr
  Register #(.width(32)) X9 (.D(RegDataW), .en(and_10_out), .clk(clocks_1_out_1), .Q(X9_q));  // open: clr
  Register #(.width(32)) X10 (.D(RegDataW), .en(and_11_out), .clk(clocks_1_out_1), .Q(X10_q));  // open: clr
  Register #(.width(32)) X11 (.D(RegDataW), .en(and_12_out), .clk(clocks_1_out_1), .Q(X11_q));  // open: clr
  Register #(.width(32)) X12 (.D(RegDataW), .en(and_13_out), .clk(clocks_1_out_1), .Q(X12_q));  // open: clr
  Register #(.width(32)) X13 (.D(RegDataW), .en(and_14_out), .clk(clocks_1_out_1), .Q(X13_q));  // open: clr
  Register #(.width(32)) X14 (.D(RegDataW), .en(and_15_out), .clk(clocks_1_out_1), .Q(X14_q));  // open: clr
  Register #(.width(32)) X15 (.D(RegDataW), .en(and_16_out), .clk(clocks_1_out_1), .Q(X15_q));  // open: clr
  Register #(.width(32)) X16 (.D(RegDataW), .en(and_17_out), .clk(clocks_1_out_1), .Q(X16_q));  // open: clr
  Register #(.width(32)) X17 (.D(RegDataW), .en(and_18_out), .clk(clocks_1_out_1), .Q(X17_q));  // open: clr
  Register #(.width(32)) X18 (.D(RegDataW), .en(and_19_out), .clk(clocks_1_out_1), .Q(X18_q));  // open: clr
  Register #(.width(32)) X19 (.D(RegDataW), .en(and_20_out), .clk(clocks_1_out_1), .Q(X19_q));  // open: clr
  Register #(.width(32)) X20 (.D(RegDataW), .en(and_21_out), .clk(clocks_1_out_1), .Q(X20_q));  // open: clr
  Register #(.width(32)) X21 (.D(RegDataW), .en(and_22_out), .clk(clocks_1_out_1), .Q(X21_q));  // open: clr
  Register #(.width(32)) X22 (.D(RegDataW), .en(and_23_out), .clk(clocks_1_out_1), .Q(X22_q));  // open: clr
  Register #(.width(32)) X23 (.D(RegDataW), .en(and_24_out), .clk(clocks_1_out_1), .Q(X23_q));  // open: clr
  Register #(.width(32)) X24 (.D(RegDataW), .en(and_25_out), .clk(clocks_1_out_1), .Q(X24_q));  // open: clr
  Register #(.width(32)) X25 (.D(RegDataW), .en(and_26_out), .clk(clocks_1_out_1), .Q(X25_q));  // open: clr
  Register #(.width(32)) X26 (.D(RegDataW), .en(and_27_out), .clk(clocks_1_out_1), .Q(X26_q));  // open: clr
  Register #(.width(32)) X27 (.D(RegDataW), .en(and_28_out), .clk(clocks_1_out_1), .Q(X27_q));  // open: clr
  Register #(.width(32)) X28 (.D(RegDataW), .en(and_29_out), .clk(clocks_1_out_1), .Q(X28_q));  // open: clr
  Register #(.width(32)) X29 (.D(RegDataW), .en(and_30_out), .clk(clocks_1_out_1), .Q(X29_q));  // open: clr
  Register #(.width(32)) X30 (.D(RegDataW), .en(and_31_out), .clk(clocks_1_out_1), .Q(X30_q));  // open: clr
  Register #(.width(32)) X31 (.D(RegDataW), .clk(clocks_1_out_1), .Q(X31_q));  // open: en, clr
  Multiplexer #(.select(5), .width(32)) multiplexer_1 (
    .in0(X0_q), .in1(X1_q), .in2(X2_q), .in3(X3_q), .in4(X4_q), .in5(X5_q), .in6(X6_q), .in7(X7_q),
    .in8(X8_q), .in9(X9_q), .in10(X10_q), .in11(X11_q), .in12(X12_q), .in13(X13_q), .in14(X14_q),
    .in15(X15_q), .in16(X16_q), .in17(X17_q), .in18(X18_q), .in19(X19_q), .in20(X20_q), .in21(X21_q),
    .in22(X22_q), .in23(X23_q), .in24(X24_q), .in25(X25_q), .in26(X26_q), .in27(X27_q), .in28(X28_q),
    .in29(X29_q), .in30(X30_q), .in31(X31_q), .out(RegData1), .sel(ReadReg1));
  Multiplexer #(.select(5), .width(32)) multiplexer_2 (
    .in0(X0_q), .in1(X1_q), .in2(X2_q), .in3(X3_q), .in4(X4_q), .in5(X5_q), .in6(X6_q), .in7(X7_q),
    .in8(X8_q), .in9(X9_q), .in10(X10_q), .in11(X11_q), .in12(X12_q), .in13(X13_q), .in14(X14_q),
    .in15(X15_q), .in16(X16_q), .in17(X17_q), .in18(X18_q), .in19(X19_q), .in20(X20_q), .in21(X21_q),
    .in22(X22_q), .in23(X23_q), .in24(X24_q), .in25(X25_q), .in26(X26_q), .in27(X27_q), .in28(X28_q),
    .in29(X29_q), .in30(X30_q), .in31(X31_q), .out(RegData2), .sel(ReadReg2));
endmodule

module Clocks (
  output out_1
);

  Clock #(.highDuration(2), .lowDuration(2)) clock_1 (.out(out_1));
endmodule

module IFID (
  input  [10:0] opcode,
  input  [10:0] imm,
  input  [4:0] Rd,
  input  [4:0] Rt,
  input  [4:0] Rm,
  input  [4:0] Rn,
  input  [10:0] PC,
  input  [10:0] nextPC,
  output [10:0] out_opcode,
  output [10:0] out_imm,
  output [4:0] out_Rd,
  output [4:0] out_Rt,
  output [4:0] out_Rm,
  output [4:0] out_Rn,
  output [10:0] out_PC,
  output [10:0] out_nextPC
);

  wire clocks_1_out_1;

  Clocks clocks_1 (.out_1(clocks_1_out_1));
  Register #(.width(11)) register_1 (.D(opcode), .en(1'b1), .clk(clocks_1_out_1), .Q(out_opcode));  // open: clr
  Register #(.width(11)) register_2 (.D(imm), .en(1'b1), .clk(clocks_1_out_1), .Q(out_imm));  // open: clr
  Register #(.width(5)) register_3 (.D(Rd), .en(1'b1), .clk(clocks_1_out_1), .Q(out_Rd));  // open: clr
  Register #(.width(5)) register_4 (.D(Rt), .en(1'b1), .clk(clocks_1_out_1), .Q(out_Rt));  // open: clr
  Register #(.width(5)) register_5 (.D(Rm), .en(1'b1), .clk(clocks_1_out_1), .Q(out_Rm));  // open: clr
  Register #(.width(5)) register_6 (.D(Rn), .en(1'b1), .clk(clocks_1_out_1), .Q(out_Rn));  // open: clr
  Register #(.width(11)) register_7 (.D(PC), .en(1'b1), .clk(clocks_1_out_1), .Q(out_PC));  // open: clr
  Register #(.width(11)) register_8 (.D(nextPC), .en(1'b1), .clk(clocks_1_out_1), .Q(out_nextPC));  // open: clr
endmodule

module IDEX (
  input  [10:0] opcode,
  input  [10:0] imm,
  input  [4:0] WriteReg,
  input  [31:0] RegData1,
  input  [31:0] RegData2,
  input  [4:0] ReadReg1,
  input  [4:0] ReadReg2,
  input  [10:0] PC,
  input  [10:0] nextPC,
  input  ALUsrc,
  input  [2:0] ALUop,
  input  UBr,
  input  CBr,
  input  PBr,
  input  MemWrite,
  input  MemRead,
  input  LinkReg,
  input  RegWrite,
  output [10:0] out_opcode,
  output [10:0] out_imm,
  output [4:0] out_WriteReg,
  output [31:0] out_RegData1,
  output [31:0] out_RegData2,
  output [4:0] out_ReadReg1,
  output [4:0] out_ReadReg2,
  output [10:0] out_PC,
  output [10:0] out_nextPC,
  output out_ALUsrc,
  output [2:0] out_ALUop,
  output out_UBr,
  output out_CBr,
  output out_PBr,
  output [1:0] out_ME,
  output [2:0] out_WB
);

  wire clocks_1_out_1;

  Clocks clocks_1 (.out_1(clocks_1_out_1));
  Register #(.width(11)) register_1 (.D(opcode), .en(1'b1), .clk(clocks_1_out_1), .Q(out_opcode));  // open: clr
  Register #(.width(11)) register_2 (.D(imm), .en(1'b1), .clk(clocks_1_out_1), .Q(out_imm));  // open: clr
  Register #(.width(5)) register_3 (.D(WriteReg), .en(1'b1), .clk(clocks_1_out_1), .Q(out_WriteReg));  // open: clr
  Register #(.width(32)) register_4 (.D(RegData1), .en(1'b1), .clk(clocks_1_out_1), .Q(out_RegData1));  // open: clr
  Register #(.width(32)) register_5 (.D(RegData2), .en(1'b1), .clk(clocks_1_out_1), .Q(out_RegData2));  // open: clr
  Register #(.width(5)) register_6 (.D(ReadReg1), .en(1'b1), .clk(clocks_1_out_1), .Q(out_ReadReg1));  // open: clr
  Register #(.width(5)) register_7 (.D(ReadReg2), .en(1'b1), .clk(clocks_1_out_1), .Q(out_ReadReg2));  // open: clr
  Register #(.width(11)) register_8 (.D(PC), .en(1'b1), .clk(clocks_1_out_1), .Q(out_PC));  // open: clr
  Register #(.width(11)) register_9 (.D(nextPC), .en(1'b1), .clk(clocks_1_out_1), .Q(out_nextPC));  // open: clr
  Register #(.width(7)) register_10 (
    .D({PBr, CBr, UBr, ALUop, ALUsrc}), .en(1'b1), .clk(clocks_1_out_1),
    .Q({out_PBr, out_CBr, out_UBr, out_ALUop, out_ALUsrc}));  // open: clr
  Register #(.width(2)) register_11 (
    .D({MemRead, MemWrite}), .en(1'b1), .clk(clocks_1_out_1), .Q(out_ME));  // open: clr
  Register #(.width(3)) register_12 (
    .D({RegWrite, LinkReg, MemRead}), .en(1'b1), .clk(clocks_1_out_1), .Q(out_WB));  // open: clr
endmodule

module EXME (
  input  [4:0] WriteReg,
  input  [31:0] ALUout,
  input  [31:0] RegData2,
  input  [10:0] nextPC,
  input  [1:0] ME,
  input  [2:0] WB,
  output [4:0] out_WriteReg,
  output [31:0] out_ALUout,
  output [31:0] out_RegData2,
  output [10:0] out_nextPC,
  output out_MemWrite,
  output out_MemRead,
  output [2:0] out_WB
);

  wire clocks_1_out_1;

  Clocks clocks_1 (.out_1(clocks_1_out_1));
  Register #(.width(5)) register_1 (.D(WriteReg), .en(1'b1), .clk(clocks_1_out_1), .Q(out_WriteReg));  // open: clr
  Register #(.width(32)) register_2 (.D(ALUout), .en(1'b1), .clk(clocks_1_out_1), .Q(out_ALUout));  // open: clr
  Register #(.width(32)) register_3 (.D(RegData2), .en(1'b1), .clk(clocks_1_out_1), .Q(out_RegData2));  // open: clr
  Register #(.width(11)) register_4 (.D(nextPC), .en(1'b1), .clk(clocks_1_out_1), .Q(out_nextPC));  // open: clr
  Register #(.width(2)) register_5 (
    .D(ME), .en(1'b1), .clk(clocks_1_out_1), .Q({out_MemRead, out_MemWrite}));  // open: clr
  Register #(.width(3)) register_6 (.D(WB), .en(1'b1), .clk(clocks_1_out_1), .Q(out_WB));  // open: clr
endmodule

module MEWB (
  input  [4:0] WriteReg,
  input  [31:0] ALUout,
  input  [31:0] ReadDataM,
  input  [10:0] nextPC,
  input  [2:0] WB,
  output [4:0] out_WriteReg,
  output [31:0] out_ALUout,
  output [31:0] out_ReadDataM,
  output [10:0] out_nextPC,
  output out_MemToReg,
  output out_LinkReg,
  output out_RegWrite
);

  wire clocks_1_out_1;

  Clocks clocks_1 (.out_1(clocks_1_out_1));
  Register #(.width(5)) register_1 (.D(WriteReg), .en(1'b1), .clk(clocks_1_out_1), .Q(out_WriteReg));  // open: clr
  Register #(.width(32)) register_2 (.D(ALUout), .en(1'b1), .clk(clocks_1_out_1), .Q(out_ALUout));  // open: clr
  Register #(.width(32)) register_3 (.D(ReadDataM), .en(1'b1), .clk(clocks_1_out_1), .Q(out_ReadDataM));  // open: clr
  Register #(.width(11)) register_4 (.D(nextPC), .en(1'b1), .clk(clocks_1_out_1), .Q(out_nextPC));  // open: clr
  Register #(.width(3)) register_5 (
    .D(WB), .en(1'b1), .clk(clocks_1_out_1), .Q({out_RegWrite, out_LinkReg, out_MemToReg}));  // open: clr
endmodule

module Control_Unit (
  input  [10:0] opcode,
  output LinkReg,
  output RegWrite,
  output MemWrite,
  output MemRead,
  output Reg2Loc,
  output [2:0] ALUop,
  output UBr,
  output CBr,
  output PBr
);


  assign ALUop = opcode[7:5];
  assign CBr = opcode[9];
  assign LinkReg = opcode[0];
  assign MemRead = opcode[3];
  assign MemWrite = opcode[2];
  assign PBr = opcode[10];
  assign Reg2Loc = opcode[4];
  assign RegWrite = opcode[1];
  assign UBr = opcode[8];
endmodule

module ALU (
  input  [3:0] action,
  input  [31:0] A,
  input  [31:0] B,
  output [31:0] ALUout,
  output Z
);

  wire comparator_1_eq, comparator_2_eq, comparator_3_eq, or_2_out;
  wire [31:0] adder_1_out, and_1_out, multiplexer_1_out, or_1_out, subtractor_1_out;

  Adder #(.width(32)) adder_1 (.a(A), .b(B), .out(adder_1_out));  // open: cin, cout
  Subtractor #(.width(32)) subtractor_1 (.a(A), .b(B), .out(subtractor_1_out));  // open: bin, bout
  assign and_1_out = A & B;  // AND_Gate and_1, 32 bits wide
  assign or_1_out = A | B;  // OR_Gate or_1, 32 bits wide
  Multiplexer #(.select(2), .width(32)) multiplexer_1 (
    .in0(and_1_out), .in1(or_1_out), .in2(adder_1_out), .in3(subtractor_1_out), .out(multiplexer_1_out),
    .sel(action[1:0]));
  Multiplexer #(.width(32)) multiplexer_2 (.in0(multiplexer_1_out), .in1(B), .out(ALUout), .sel(action[2]));
  Comparator #(.width(32)) comparator_1 (.a(adder_1_out), .b(multiplexer_1_out), .eq(comparator_1_eq));  // open: gt, lt
  Comparator #(.width(32)) comparator_2 (
    .a(multiplexer_1_out), .b(subtractor_1_out), .eq(comparator_2_eq));  // open: gt, lt
  Comparator #(.width(32)) comparator_3 (.a(and_1_out), .b(multiplexer_1_out), .eq(comparator_3_eq));  // open: gt, lt
  or or_2 (or_2_out, comparator_1_eq, comparator_2_eq, comparator_3_eq);
  assign Z = action[3] ? or_2_out : 1'bz;  // Controlled_Buffer controlled_buffer_1
endmodule

module ALU_Control (
  input  [2:0] ALUop,
  output [3:0] action
);

  Multiplexer #(.select(3), .width(4)) multiplexer_1 (
    .in0(4'b0000), .in1(4'b0001), .in2(4'b0010), .in3(4'b0011), .in4(4'b0111), .in5(4'b1000), .in6(4'b1010),
    .in7(4'b1011), .out(action), .sel(ALUop));
endmodule

module Hazard_Detection_Unit (
  input  [4:0] IFID_ReadReg1,
  input  [4:0] IDEX_WriteReg,
  input  [4:0] IFID_ReadReg2,
  input  IDEX_MemRead,
  input  IDEX_Br,
  output HazardSignal
);

  wire and_1_out, comparator_1_eq, comparator_2_eq, or_1_out;

  Comparator #(.mode("unsigned"), .width(5)) comparator_1 (
    .a(IFID_ReadReg1), .b(IDEX_WriteReg), .eq(comparator_1_eq));  // open: gt, lt
  Comparator #(.mode("unsigned"), .width(5)) comparator_2 (
    .a(IDEX_WriteReg), .b(IFID_ReadReg2), .eq(comparator_2_eq));  // open: gt, lt
  or or_1 (or_1_out, comparator_1_eq, comparator_2_eq);
  and and_1 (and_1_out, or_1_out, IDEX_MemRead);
  or or_2 (HazardSignal, and_1_out, IDEX_Br);
endmodule

module Forwarding_Unit (
  input  EXME_RegWrite,
  input  [4:0] EXME_WriteReg,
  input  [4:0] IDEX_ReadReg1,
  input  [4:0] MEWB_WriteReg,
  input  MEWB_RegWrite,
  input  [4:0] IDEX_ReadReg2,
  output [1:0] FA,
  output [1:0] FB
);

  wire and_1_out, and_2_out, and_3_out, and_4_out, comparator_1_eq, comparator_2_eq, comparator_3_eq,
       comparator_4_eq, comparator_5_eq, comparator_6_eq, comparator_7_eq, comparator_8_eq, not_1_out,
       not_2_out, not_3_out, not_4_out;
  wire [1:0] multiplexer_1_out, multiplexer_2_out;

  Comparator #(.width(5)) comparator_1 (.a({5{1'b1}}), .b(EXME_WriteReg), .eq(comparator_1_eq));  // open: gt, lt
  Comparator #(.width(5)) comparator_2 (.a(EXME_WriteReg), .b(IDEX_ReadReg1), .eq(comparator_2_eq));  // open: gt, lt
  Comparator #(.width(5)) comparator_3 (.a(IDEX_ReadReg1), .b(MEWB_WriteReg), .eq(comparator_3_eq));  // open: gt, lt
  Comparator #(.width(5)) comparator_4 (.a(MEWB_WriteReg), .b({5{1'b1}}), .eq(comparator_4_eq));  // open: gt, lt
  Comparator #(.width(5)) comparator_5 (.a({5{1'b1}}), .b(EXME_WriteReg), .eq(comparator_5_eq));  // open: gt, lt
  Comparator #(.width(5)) comparator_6 (.a(EXME_WriteReg), .b(IDEX_ReadReg2), .eq(comparator_6_eq));  // open: gt, lt
  Comparator #(.width(5)) comparator_7 (.a(IDEX_ReadReg2), .b(MEWB_WriteReg), .eq(comparator_7_eq));  // open: gt, lt
  Comparator #(.width(5)) comparator_8 (.a(MEWB_WriteReg), .b({5{1'b1}}), .eq(comparator_8_eq));  // open: gt, lt
  not not_1 (not_1_out, comparator_1_eq);
  not not_2 (not_2_out, comparator_4_eq);
  not not_3 (not_3_out, comparator_5_eq);
  not not_4 (not_4_out, comparator_8_eq);
  and and_1 (and_1_out, not_1_out, EXME_RegWrite, comparator_2_eq);
  and and_2 (and_2_out, comparator_3_eq, MEWB_RegWrite, not_2_out);
  and and_3 (and_3_out, not_3_out, EXME_RegWrite, comparator_6_eq);
  and and_4 (and_4_out, comparator_7_eq, MEWB_RegWrite, not_4_out);
  Multiplexer #(.width(2)) multiplexer_1 (.in0(2'b00), .in1(2'b10), .out(multiplexer_1_out), .sel(and_2_out));
  Multiplexer #(.width(2)) multiplexer_2 (.in0(2'b00), .in1(2'b10), .out(multiplexer_2_out), .sel(and_4_out));
  Multiplexer #(.width(2)) multiplexer_3 (.in0(multiplexer_1_out), .in1(2'b01), .out(FA), .sel(and_1_out));
  Multiplexer #(.width(2)) multiplexer_4 (.in0(multiplexer_2_out), .in1(2'b01), .out(FB), .sel(and_3_out));
endmodule
